// Logisim project Circuitos-logi.circ as structural Verilog: 1 circuit, main circuit main
module main (
  input  i0,
  input  i1,
  input  s0,
  input  s1,
  output out0,
  output out1
);

  Multiplexer multiplexer_1 (.in0(i0), .in1(i1), .out(out0), .sel(s0));  // open: en
  Multiplexer multiplexer_2 (.in0(i0), .in1(i1), .out(out1), .sel(s1));  // open: en
endmodule
